// Digital circuit 16-bit ALU.dig as structural Verilog
module _16_bit_ALU (
  input  F2,
  input  F1,
  input  F0,
  input  Cin,
  input  A0,
  input  B0,
  input  A1,
  input  B1,
  input  A2,
  input  B2,
  input  A3,
  input  B3,
  input  A4,
  input  B4,
  input  A5,
  input  B5,
  input  A6,
  input  B6,
  input  A7,
  input  B7,
  input  A8,
  input  B8,
  input  A9,
  input  B9,
  input  A10,
  input  B10,
  input  A11,
  input  B11,
  input  A12,
  input  B12,
  input  A13,
  input  B13,
  input  A14,
  input  B14,
  input  A15,
  input  B15,
  output Q0,
  output Cout,
  output Q1,
  output Q2,
  output Q3,
  output Q4,
  output Q5,
  output Q6,
  output Q7,
  output Q8,
  output Q9,
  output Q10,
  output Q11,
  output Q12,
  output Q13,
  output Q14,
  output Q15
);

  wire alu_2_cout, alu_3_cout, alu_4_cout, alu_5_cout, alu_6_cout, alu_7_cout, alu_8_cout, alu_9_cout,
       alu_10_cout, alu_11_cout, alu_12_cout, alu_13_cout, alu_14_cout, alu_15_cout, alu_16_cout;

  ALU alu_1 (.A(F2), .B(F1), .F2(F0), .F1(alu_2_cout), .F0(B15), .Cin(A15), .Q(Q15), .Cout(Cout));
  ALU alu_2 (.A(F2), .B(F1), .F2(F0), .F1(alu_3_cout), .F0(B14), .Cin(A14), .Q(Q14), .Cout(alu_2_cout));
  ALU alu_3 (.A(F2), .B(F1), .F2(F0), .F1(alu_4_cout), .F0(B13), .Cin(A13), .Q(Q13), .Cout(alu_3_cout));
  ALU alu_4 (.A(F2), .B(F1), .F2(F0), .F1(alu_5_cout), .F0(B12), .Cin(A12), .Q(Q12), .Cout(alu_4_cout));
  ALU alu_5 (.A(F2), .B(F1), .F2(F0), .F1(alu_6_cout), .F0(B11), .Cin(A11), .Q(Q11), .Cout(alu_5_cout));
  ALU alu_6 (.A(F2), .B(F1), .F2(F0), .F1(alu_7_cout), .F0(B10), .Cin(A10), .Q(Q10), .Cout(alu_6_cout));
  ALU alu_7 (.A(F2), .B(F1), .F2(F0), .F1(alu_8_cout), .F0(B9), .Cin(A9), .Q(Q9), .Cout(alu_7_cout));
  ALU alu_8 (.A(F2), .B(F1), .F2(F0), .F1(alu_9_cout), .F0(B8), .Cin(A8), .Q(Q8), .Cout(alu_8_cout));
  ALU alu_9 (.A(F2), .B(F1), .F2(F0), .F1(alu_10_cout), .F0(B7), .Cin(A7), .Q(Q7), .Cout(alu_9_cout));
  ALU alu_10 (.A(F2), .B(F1), .F2(F0), .F1(alu_11_cout), .F0(B6), .Cin(A6), .Q(Q6), .Cout(alu_10_cout));
  ALU alu_11 (.A(F2), .B(F1), .F2(F0), .F1(alu_12_cout), .F0(B5), .Cin(A5), .Q(Q5), .Cout(alu_11_cout));
  ALU alu_12 (.A(F2), .B(F1), .F2(F0), .F1(alu_13_cout), .F0(B4), .Cin(A4), .Q(Q4), .Cout(alu_12_cout));
  ALU alu_13 (.A(F2), .B(F1), .F2(F0), .F1(alu_14_cout), .F0(B3), .Cin(A3), .Q(Q3), .Cout(alu_13_cout));
  ALU alu_14 (.A(F2), .B(F1), .F2(F0), .F1(alu_15_cout), .F0(B2), .Cin(A2), .Q(Q2), .Cout(alu_14_cout));
  ALU alu_15 (.A(F2), .B(F1), .F2(F0), .F1(alu_16_cout), .F0(B1), .Cin(A1), .Q(Q1), .Cout(alu_15_cout));
  ALU alu_16 (.A(F2), .B(F1), .F2(F0), .F1(Cin), .F0(B0), .Cin(A0), .Q(Q0), .Cout(alu_16_cout));
endmodule
