// Digital circuit ALU.dig as structural Verilog
module ALU (
  input  A,
  input  B,
  input  F2,
  input  F1,
  input  F0,
  input  Cin,
  output Q,
  output Cout
);

  wire add_1_c_o, add_1_s, and_1_out, multiplexer_1_out, multiplexer_3_out, multiplexer_4_out, not_1_out,
       or_1_out, sub_1_c_o, sub_1_s;

  Add add_1 (.a(A), .b(B), .c_i(Cin), .s(add_1_s), .c_o(add_1_c_o));
  Sub sub_1 (.a(A), .b(B), .c_i(Cin), .s(sub_1_s), .c_o(sub_1_c_o));
  and and_1 (and_1_out, B, A);
  not not_1 (not_1_out, A);
  Multiplexer multiplexer_1 (.sel(F0), .in_0(A), .in_1(not_1_out), .out(multiplexer_1_out));
  Multiplexer multiplexer_2 (.sel(F2), .in_0(add_1_c_o), .in_1(sub_1_c_o), .out(Cout));
  Multiplexer multiplexer_3 (.sel(F1), .in_0(and_1_out), .in_1(multiplexer_1_out), .out(multiplexer_3_out));
  Multiplexer multiplexer_4 (.sel(F2), .in_0(add_1_s), .in_1(sub_1_s), .out(multiplexer_4_out));
  or or_1 (or_1_out, F1, F0);
  Multiplexer multiplexer_5 (.sel(or_1_out), .in_0(multiplexer_4_out), .in_1(multiplexer_3_out), .out(Q));
endmodule

/* Test case ALU:
F2 F1 F0 Cin A B  Q Cout
0 0 0 0 0 0  0 0
0 0 0 0 0 1  1 0
0 0 0 0 1 0  1 0
0 0 0 0 1 1  0 1
0 0 0 1 0 0  1 0
0 0 0 1 0 1  0 1
0 0 0 1 1 0  0 1
0 0 0 1 1 1  1 1
0 0 1 0 0 0  0 0
0 0 1 0 0 1  0 0
0 0 1 0 1 0  0 0
0 0 1 0 1 1  1 1
0 0 1 1 0 0  0 0
0 0 1 1 0 1  0 1
0 0 1 1 1 0  0 1
0 0 1 1 1 1  1 1
0 1 0 0 0 0  0 0
0 1 0 0 0 1  0 0
0 1 0 0 1 0  1 0
0 1 0 0 1 1  1 1
0 1 0 1 0 0  0 0
0 1 0 1 0 1  0 1
0 1 0 1 1 0  1 1
0 1 0 1 1 1  1 1
0 1 1 0 0 0  1 0
0 1 1 0 0 1  1 0
0 1 1 0 1 0  0 0
0 1 1 0 1 1  0 1
0 1 1 1 0 0  1 0
0 1 1 1 0 1  1 1
0 1 1 1 1 0  0 1
0 1 1 1 1 1  0 1
1 0 0 0 0 0  0 0
1 0 0 0 0 1  1 1
1 0 0 0 1 0  1 0
1 0 0 0 1 1  0 0
1 0 0 1 0 0  1 1
1 0 0 1 0 1  0 1
1 0 0 1 1 0  0 0
1 0 0 1 1 1  1 1
*/
